# Fritzing sketch fi-apartmentbot (saved by Fritzing 0.3.14b)
breadboards: 1

parts:
  U1 = 3-Axis Accelerometer Breakout
  J1 = Infrared Proximity Sensor
  J2 = Basic Servo
  J3 = Basic Servo
  Arduino1 = Arduino

nets:
  N1: U1.Z, Arduino1.A3
  N2: U1.Y, Arduino1.A2
  N3: U1.X, Arduino1.A1
  N4: J1.Vout, Arduino1.D7
  GND: J1.GND, J2.gnd, J3.gnd
  VCC: J1.Vcc, J2.vcc, J3.vcc
  N5: J2.pulse, Arduino1.D5
  N6: J3.pulse, Arduino1.D6
